# Fritzing sketch luminaire-demiarc (saved by Fritzing 0.9.3b)
breadboards: 1

parts:
  U1 = attiny85 [package=dip]
  U3 = POT_SWITCH [package=pot_pth]
  NEOPIXEL1 = Neopixel Strip -- White (60/m) [part_number=1138]
  JACK1 = 2.1mm Barrel Jack with Terminal Block
  R4 = Resistor [tolerance=±5% resistance=390 package="0805 [SMD]"]
  C3 = Capacitor Polarized [package=cpol-radial-10uf-25v]
  R5 = Resistor [tolerance=±5% resistance=390 package="0805 [SMD]"]

nets:
  N1: U1.Pin_2, U3.G$2_2, R4.Pin_1
  N2: U1.Pin_4, U3.G$1_A, NEOPIXEL1.GND, JACK1.NEG, R4.Pin_0, C3.-
  N3: U1.Pin_5, R5.Pin_0
  N4: U1.Pin_7, U3.G$2_1
  N5: U1.Pin_8, U3.G$1_E, U3.G$1_S, NEOPIXEL1.+5V, C3.+
  N6: NEOPIXEL1.DI, R5.Pin_1

notes:
  10mF
  POTENTIOMETER WITH ON/OFF SWITCH INTEGRATED
  ATTINY85 + WS2812
  green ATTiny pin A3
  green to ATTiny pin A1
  green to ATTiny pin 0

custom parts:
  Neopixel Strip -- White (60/m): Neopixel Strip, White, 60 pixels per meter.
